# Fritzing sketch Asg1 (saved by Fritzing 0.9.3b)
breadboards: 1

parts:
  U1 = NodeMCU V1.0
  Part1 = KY-037 High Sensitivity Sound Detection Module [package="Breakout board"]
  OLED_I2C1 = OLED 128x64 I2C Monochrome Display
  A1 = DHT22 module

nets:
  N1: U1.D1, OLED_I2C1.SCK
  N2: U1.D2, OLED_I2C1.SDA
  3V3: U1.3V3, Part1.+, OLED_I2C1.VDD, A1.VCC
  GND: U1.GND, Part1.G, OLED_I2C1.GND, A1.GND
  N3: U1.D5, A1.DAT
  N4: U1.D6, Part1.D0

custom parts:
  NodeMCU V1.0: ESP8266 based NodeMCU
  KY-037 High Sensitivity Sound Detection Module: KY-037 high sensitivity sound detection module is an analog/digital sensor that uses a condenser microphone to observe changes in environment noise.
  DHT22 module: DHT22 module. Pins GND VCC Data.
